// Digital circuit SPIMaster.dig as structural Verilog
module SPIMaster (
  input  nRES,
  input  MISO,
  input  D_0,
  input  D_1,
  input  D_2,
  input  D_3,
  input  D_4,
  input  D_5,
  input  D_6,
  input  D_7,
  input  nCE,
  input  A_0,
  input  RnW,
  input  VCC,
  input  GND,
  input  clk,
  output MOSI,
  output nCS_0,
  output nCS_1,
  output nCS_2,
  output nCS_3,
  output nIRQ,
  output SPICLK,
  output CLK_2
);

  wire and_1_out, DEN, DIV_0, DIV_1, DIVCLK, IEN, ITC, nCTRL_RD, nCTRL_WR, nDATA_RD, nDATA_WR, not_1_out,
       not_2_out, not_3_out, nSAFEDATA_WR, nTXC, RES, RUNNING, SEL_0, SEL_1, SEROUT, TXC;

  PowerSupply powersupply_1 (.VDD(VCC), .GND(GND));
  StateMachine statemachine_1 (.SPI_CLK(SPICLK), .TXC(TXC), .CLK(DIVCLK), .nRES(nRES), .RUNNING(RUNNING));
  DataRegister dataregister_1 (
    .CLK(SPICLK), .nRD(nDATA_RD), .nWR(nSAFEDATA_WR), .D_0(D_0), .D_1(D_1), .D_2(D_2), .D_3(D_3), .D_4(D_4),
    .D_5(D_5), .D_6(D_6), .D_7(D_7), .MISO(MISO), .TXC(TXC), .MOSI(SEROUT));
  // ControlRegister controlregister_1: pin names not known; wires that end beside it: D_0, D_1, D_2, D_3, D_4, D_5, D_6, D_7, nRES, nCTRL_WR, nCTRL_RD, nSAFEDATA_WR, GND, VCC, RUNNING, DIV_0, DIV_1, SEL_0, SEL_1, DEN, IEN, ITC
  and and_1 (and_1_out, nDATA_WR, nDATA_RD);
  nand nand_1 (nSAFEDATA_WR, clk, not_1_out);
  not not_1 (not_1_out, nDATA_WR);
  not not_2 (not_2_out, SEROUT);
  not not_3 (not_3_out, DEN);
  nand nand_2 (nIRQ, ITC, IEN);
  not not_4 (nTXC, TXC);
  not not_5 (RES, nRES);
  nand nand_3 (MOSI, RUNNING, not_2_out);
  ClockSelect clockselect_1 (.DIV0(DIV_0), .DIV1(DIV_1), .CLK(clk), .RES(RES), .DIV_CLK(DIVCLK));
  _74139 Device___Register_Select (
    .pin1(not_3_out), .pin2(SEL_0), .pin3(SEL_1), .pin4(nCS_0), .pin5(nCS_1), .pin6(nCS_2), .pin7(nCS_3),
    .pin8(GND), .pin9(nCTRL_RD), .pin10(nCTRL_WR), .pin11(nDATA_RD), .pin12(nDATA_WR), .pin13(A_0),
    .pin14(RnW), .pin15(nCE), .pin16(VCC));

  assign CLK_2 = clk;

  // Notes on the sheet:
  //   nCE: default 1
  //   nCS_0: pin 4
  //   nCS_1: pin 5
  //   nCS_2: pin 6
  //   nCS_3: pin 7
  //   RnW: default 1
  //   VCC: default 1
  //   Real device doesn't need to reset
  //   this clock select circuit. If positive
  //   reset isn't needed except for this
  //   we can skip generating that signal.
endmodule
