// Digital circuit StateMachine.dig as structural Verilog
module StateMachine (
  input  CLK,
  input  CLR,
  output TXC,
  output SPI_CLK
);

  _74HC393 _74hc393_1 ();
  _74HC393 _74hc393_2 ();

  // Notes on the sheet:
  //   TXC: pin 5
  //   CLK: pin 1
  //   SPI_CLK: pin 7
endmodule

/* Test case:
CLK ~RES TXC
0   1    0
C   1    0
C   1    0
C   1    0
C   1    0
C   1    0
C   1    0
C   1    0
C   1    1
*/
